# Fritzing sketch rpi3_schematics (saved by Fritzing 0.9.3b)
breadboards: 1

parts:
  S1 = Pushbutton [package="[THT]"]
  OLED_I2C1 = OLED 128x64 I2C Monochrome Display
  Raspberry_Pi_1 = Raspberry Pi 3 [part_number=RPI-3-V1.2]
  J1 = Basic Servo
  R1 = Resistor [tolerance=±5% resistance=220 package=THT]
  LED1 = LED - 5mm [color="Red (633nm)" package="5 mm [THT]"]
  R2 = Resistor [tolerance=±5% resistance=220 package=THT]

nets:
  N1: S1.Pin_1, S1.Pin_2, R2.Pin_1
  GND: S1.Pin_3, S1.Pin_4, OLED_I2C1.GND, Raspberry_Pi_1.GND, J1.gnd
  N2: OLED_I2C1.SDA, Raspberry_Pi_1.GPIO2
  N3: OLED_I2C1.SCK, Raspberry_Pi_1.GPIO3
  VDD: OLED_I2C1.VDD, Raspberry_Pi_1.5V, J1.vcc, LED1.cathode
  N4: Raspberry_Pi_1.GPIO22, R2.Pin_0
  N5: Raspberry_Pi_1.GPIO6, R1.Pin_0
  N6: Raspberry_Pi_1.GPIO18, J1.pulse
  N7: R1.Pin_1, LED1.anode
